# Fritzing sketch balcon_irrigation_circuits (saved by Fritzing 0.9.4)
circuit board: 8.46667cm x 5.64444cm
breadboards: 1

parts:
  Part1 = Arduino Uno (Rev3) - ICSP
  Capacitive_Soil_Moisture_Sensor1 = DFRobot Capacitive Soil Moisture Sensor V1.0 [part_number=SEN0193]
  M1 = DC Motor
  R1 = Resistor [tolerance=±5% resistance=470 package="0402 [SMD]"]
  BC337 = TMP36 Temperature Sensor [package="TO92 [THT]"]
  1N4148 = Diode [package=diode-1n4148]
  Capacitive_Soil_Moisture_Sensor2 = DFRobot Capacitive Soil Moisture Sensor V1.0 [part_number=SEN0193]
  Capacitive_Soil_Moisture_Sensor3 = DFRobot Capacitive Soil Moisture Sensor V1.0 [part_number=SEN0193]
  Capacitive_Soil_Moisture_Sensor4 = DFRobot Capacitive Soil Moisture Sensor V1.0 [part_number=SEN0193]
  Capacitive_Soil_Moisture_Sensor5 = DFRobot Capacitive Soil Moisture Sensor V1.0 [part_number=SEN0193]
  M2 = DC Motor
  M3 = DC Motor
  M4 = DC Motor
  M5 = DC Motor
  R2 = Resistor [tolerance=±5% resistance=470 package="0402 [SMD]"]
  R3 = Resistor [tolerance=±5% resistance=470 package="0402 [SMD]"]
  R4 = Resistor [tolerance=±5% resistance=470 package="0402 [SMD]"]
  R5 = Resistor [tolerance=±5% resistance=470 package="0402 [SMD]"]
  T2 = TMP36 Temperature Sensor [package="TO92 [THT]"]
  T3 = TMP36 Temperature Sensor [package="TO92 [THT]"]
  T4 = TMP36 Temperature Sensor [package="TO92 [THT]"]
  T5 = TMP36 Temperature Sensor [package="TO92 [THT]"]
  D2 = Diode [package=diode-1n4148]
  D3 = Diode [package=diode-1n4148]
  D4 = Diode [package=diode-1n4148]
  D5 = Diode [package=diode-1n4148]

nets:
  N1: Part1.A1, Capacitive_Soil_Moisture_Sensor1.A
  N2: Part1.A2, Capacitive_Soil_Moisture_Sensor2.A
  N3: Part1.A3, Capacitive_Soil_Moisture_Sensor5.A
  N4: Part1.A4/SDA, Capacitive_Soil_Moisture_Sensor4.A
  N5: Part1.A5/SCL, Capacitive_Soil_Moisture_Sensor3.A
  GND: Part1.GND, Capacitive_Soil_Moisture_Sensor1.GND, BC337.GND, Capacitive_Soil_Moisture_Sensor2.GND, Capacitive_Soil_Moisture_Sensor3.GND, Capacitive_Soil_Moisture_Sensor4.GND, Capacitive_Soil_Moisture_Sensor5.GND, T2.GND, T3.GND, T4.GND, T5.GND
  N6: Part1.D9_PWM, R5.Pin_0, R5.Pin_1, T5.Vout
  N7: Part1.D10_PWM/SS, R4.Pin_0, R4.Pin_1, T4.Vout
  N8: Part1.D11_PWM/MOSI, R3.Pin_0, R3.Pin_1, T3.Vout
  N9: Part1.D12/MISO, R2.Pin_0, R2.Pin_1, T2.Vout
  N10: Part1.D13/SCK, R1.Pin_0, R1.Pin_1, BC337.Vout
  VCC: Part1.5V, Capacitive_Soil_Moisture_Sensor1.VCC, M1.pin_1, 1N4148.C, Capacitive_Soil_Moisture_Sensor2.VCC, Capacitive_Soil_Moisture_Sensor3.VCC, Capacitive_Soil_Moisture_Sensor4.VCC, Capacitive_Soil_Moisture_Sensor5.VCC, M2.pin_1, M3.pin_1, M4.pin_1, M5.pin_1, D2.C, D3.C, D4.C, D5.C
  N11: M1.pin_2, BC337.+Vs, 1N4148.A
  N12: M2.pin_2, T2.+Vs, D3.A
  N13: M3.pin_2, T3.+Vs, D2.A
  N14: M4.pin_2, T4.+Vs, D4.A
  N15: M5.pin_2, T5.+Vs, D5.A

custom parts:
  DFRobot Capacitive Soil Moisture Sensor V1.0: DFRobot Capacitive Soil Moisture Sensor V1.0 This product measures soil moisture levels by capacitive sensing, rather than resistive sensing like other types of moisture sensor. It is made of a corrosion resistant material giving it a long service life. Insert it into soil and impress your friends with the real-time soil moisture data! The product includes an on-board voltage regulator which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
